# Fritzing sketch Luxio (saved by Fritzing 0.9.4)

parts:
  U1 = SK6812 RGBW LED Strip
  M1 = WeMos D1 Mini V4.0.0

nets:
  N1: U1.GND#0, M1.GND
  N2: U1.Din, U1.GND#3, M1.0
  N3: U1.+5V, M1.VBUS

custom parts:
  SK6812 RGBW LED Strip: SK6812 RGBW Strip
  WeMos D1 Mini V4.0.0: The D1 mini is a mini wifi board based on ESP-8266EX.
